// Logisim project es porte logiche 2024.circ as structural Verilog: 1 circuit, main circuit main
module main (
  input  A,
  input  B,
  input  S,
  output out_4,
  output out_5,
  output out_6
);

  wire and_1_out, and_2_out, and_3_out, and_4_out, and_5_out, and_6_out, and_7_out, and_8_out, and_9_out;

  and and_1 (and_1_out, B, S);
  and and_2 (and_2_out, A, B);
  and and_3 (and_3_out, A, ~S);  // AND_Gate
  or or_1 (out_4, and_1_out, and_2_out, and_3_out);
  and and_4 (and_4_out, ~A, B, S);  // AND_Gate
  and and_5 (and_5_out, A, ~B, ~S);  // AND_Gate
  and and_6 (and_6_out, A, B, ~S);  // AND_Gate
  and and_7 (and_7_out, A, B, S);
  or or_2 (out_6, and_4_out, and_5_out, and_6_out, and_7_out);
  and and_8 (and_8_out, B, S);
  and and_9 (and_9_out, A, ~S);  // AND_Gate
  or or_3 (out_5, and_8_out, and_9_out);
endmodule
