// Logisim project mappa 5 variabili.circ as structural Verilog: 1 circuit, main circuit main
module main (
  input  A,
  input  B,
  input  C,
  input  D,
  input  E,
  output out_6
);

  wire and_1_out, and_2_out, and_3_out, and_4_out, and_5_out, and_6_out, and_7_out, and_8_out, and_9_out,
       and_10_out, and_11_out, and_12_out, and_13_out, and_14_out, and_15_out, and_19_out, and_20_out,
       and_21_out;

  and and_1 (and_1_out, D, E, ~A);  // AND_Gate
  and and_2 (and_2_out, A, C, D);
  and and_3 (and_3_out, B, ~C, E);  // AND_Gate
  and and_4 (and_4_out, ~B, ~C, ~D, ~E);  // AND_Gate
  and and_5 (and_5_out, ~A, B, C, ~D, ~E);  // AND_Gate
  and and_6 (and_6_out, B, ~C, E);  // AND_Gate
  and and_7 (and_7_out, ~A, B, C, D);  // AND_Gate
  and and_8 (and_8_out, ~A, ~B, ~C, ~D, ~E);  // AND_Gate
  and and_9 (and_9_out, ~A, ~B, ~C, D, E);  // AND_Gate
  and and_10 (and_10_out, ~A, ~B, C, D, E);  // AND_Gate
  and and_11 (and_11_out, ~A, B, ~C, ~D, E);  // AND_Gate
  and and_12 (and_12_out, ~A, B, ~C, D, E);  // AND_Gate
  and and_13 (and_13_out, ~A, B, C, ~D, ~E);  // AND_Gate
  and and_14 (and_14_out, ~A, B, C, D, ~E);  // AND_Gate
  and and_15 (and_15_out, ~A, B, C, D, E);  // AND_Gate
  // AND_Gate and_16 has open pins: in0=A, in1=B, in2=C, in3=D, in4=E, out=open
  // AND_Gate and_17 has open pins: in0=A, in1=B, in2=C, in3=D, in4=E, out=open
  // AND_Gate and_18 has open pins: in0=A, in1=B, in2=C, in3=D, in4=E, out=open
  and and_19 (and_19_out, A, B, ~C, ~D, E);  // AND_Gate
  and and_20 (and_20_out, A, B, ~C, D, E);  // AND_Gate
  and and_21 (and_21_out, A, B, C, D, E);
  or or_1 (out_6, and_1_out, and_2_out, and_3_out, and_4_out, and_5_out, and_6_out, and_7_out);
  // OR_Gate or_2 has open pins: in0=and_8_out, in1=and_9_out, in2=and_10_out, in3=and_11_out, in4=and_12_out, in5=and_13_out, in6=and_14_out, in7=and_15_out, in12=and_19_out, in13=and_20_out, in14=and_21_out, out=open
endmodule
